# Fritzing sketch Motion Controller - Main Board (saved by Fritzing 0.9.3b)
perfboards: 1

parts:
  IC1 = MCP23017 I2C I/O Expander
  R1 = Resistor [tolerance=±5% resistance=4.7k package=THT]
  Keypad = female pin header, 8 pins [form="♀ (female)"]
  LCD_Display = female pin header, 5 pins [form="♀ (female)"]
  To_Stepper_Controller_Board = Header 5x2 [package=avr_icsp]
  Rp2 = Resistor [tolerance=±5% resistance=10k package=THT]
  Rp1 = Resistor [tolerance=±5% resistance=10k package=THT]
  U2 = NodeMCU V1.0
  DS3231_RTC = female pin header, 5 pins [form="♀ (female)"]
  Brightness = Rotary Potentiometer (Large) [maximum_resistance=100kΩ package=THT]

nets:
  5V: IC1.VDD, IC1.A1, R1.Pin_1, LCD_Display.pin2, To_Stepper_Controller_Board.5, To_Stepper_Controller_Board.9, Rp2.Pin_1, Rp1.Pin_1, U2.Vin, DS3231_RTC.pin2
  GND: IC1.VSS, IC1.A0, IC1.A2, LCD_Display.pin1, To_Stepper_Controller_Board.3, To_Stepper_Controller_Board.4, U2.GND, DS3231_RTC.pin1, Brightness.leg1
  N1: IC1.SCL, LCD_Display.pin4, Rp1.Pin_0, U2.D6, DS3231_RTC.pin4
  N2: IC1.SDA, LCD_Display.pin3, Rp2.Pin_0, U2.D5, DS3231_RTC.pin3
  N3: IC1.RESET, R1.Pin_0
  N4: IC1.GPA0, Keypad.pin8
  N5: IC1.GPA1, Keypad.pin7
  N6: IC1.GPA2, Keypad.pin6
  N7: IC1.GPA3, Keypad.pin5
  N8: IC1.GPA4, Keypad.pin4
  N9: IC1.GPA5, Keypad.pin3
  N10: IC1.GPA6, Keypad.pin2
  N11: IC1.GPA7, Keypad.pin1
  N12: LCD_Display.pin5, U2.D4
  N13: To_Stepper_Controller_Board.1, U2.D8
  N14: To_Stepper_Controller_Board.2, U2.D7
  N15: To_Stepper_Controller_Board.6, U2.D2
  N16: To_Stepper_Controller_Board.7, U2.D1
  N17: To_Stepper_Controller_Board.8, U2.D0
  N18: U2.D3, DS3231_RTC.pin5
  N19: U2.3V3, Brightness.leg2
  N20: U2.A0, Brightness.wiper

notes:
  D1 -STEP
  D2 - SLEEP
  D0 - DIR
  D7 (Yellow) - Limit Switch
  A0 - POT
  D5 - SDA
  D6 - SCL
  D3 - SQW (interupt)
  D8 - Camera
  D4 - PWM for LCD

custom parts:
  MCP23017 I2C I/O Expander: The MCP23017 uses two i2c pins (these can be shared with other i2c devices), and in exchange gives you 16 general purpose pins. You can set each of 16 pins to be input, output, input with a pullup or open drain. There's even the ability to get an interrupt via an external pin when any of the inputs change so you don't have to keep polling the chip.
  NodeMCU V1.0: ESP8266 based NodeMCU
