# Fritzing sketch Motion Controller - Stepper Control Board (saved by Fritzing 0.9.3b)

parts:
  DRV_1 = DRV 8825 Stepper Motor Carrier, High Current [part_number="DRV 8825"]
  J1 = male pin header, 4 pins [form="♂ (male)"]
  To_Mainboard = Header 5x2 [package=avr_icsp]
  To_J-Box_(check_colors) = 3.5mm Audio Jack [package=audio-jack-3.5mm-smd]

nets:
  5V: DRV_1.MS2, To_Mainboard.5, To_Mainboard.9
  N1: DRV_1.SLEEP, To_Mainboard.6
  N2: DRV_1.STEP, To_Mainboard.7
  N3: DRV_1.DIRECTION, To_Mainboard.8
  12V: DRV_1.VOLTAGE_ST/_MT
  GND: DRV_1.GROUND_ST/_MT, To_Mainboard.3, To_Mainboard.4, To_J-Box_(check_colors).SLEEVE
  N4: DRV_1.OUT_2B, J1.pin1
  N5: DRV_1.OUT_2A, J1.pin2
  N6: DRV_1.OUT_1A, J1.pin3
  N7: DRV_1.OUT_1B, J1.pin4
  N8: To_Mainboard.1, To_J-Box_(check_colors).LEFT
  N9: To_Mainboard.2, To_J-Box_(check_colors).RIGHT

notes:
  green - camera, yellow - limit switch
  note: setting MS2 to high puts driver in 1/4 step mode (labeled MS0 on mine and on datasheet))
