# Fritzing sketch j-box (saved by Fritzing 0.9.3b)
perfboards: 1

parts:
  Camera = male pin header, 3 pins [form="♂ (male)"]
  To_j-box_via_3_5mm_headphones_jack = female pin header, 3 pins [form="♀ (female)"]
  Limit_Switch_1 = male pin header, 2 pins [form="♂ (male)"]
  Limit_Switch_2 = male pin header, 2 pins [form="♂ (male)"]
  Optocoupler = Sharp PC817 [package=THT]
  R1 = Resistor [tolerance=±1% resistance=2k package=THT]

nets:
  N1: Camera.pin1, Camera.pin2, Optocoupler.Pin_3
  N2: Camera.pin3, Optocoupler.Pin_4
  N3: To_j-box_via_3_5mm_headphones_jack.pin1, R1.Pin_0
  N4: To_j-box_via_3_5mm_headphones_jack.pin2, Limit_Switch_1.pin1, Limit_Switch_2.pin1
  N5: To_j-box_via_3_5mm_headphones_jack.pin3, Limit_Switch_1.pin2, Limit_Switch_2.pin2, Optocoupler.Pin_2
  N6: Optocoupler.Pin_1, R1.Pin_1
